# Fritzing sketch Leonardo-RaspberryB (saved by Fritzing 0.8.5b)

parts:
  Composants1 = Arduino Leonardo (Rev3b)
  Raspberry_Pi_B_rev2 = Raspberry Pi B rev2

nets:
  GND: Composants1.GND, Raspberry_Pi_B_rev2.GND
  N1: Composants1.SDA, Raspberry_Pi_B_rev2.GPIO_2
  N2: Composants1.SCL, Raspberry_Pi_B_rev2.GPIO_3
